// Logisim project Computer.circ as structural Verilog
module main (
);

  wire ADDR1MUX, and_1_out, and_2_out, ASK, CKEY, Clock, GateALU, GateHDD, GateKR, GateMARMUX, GateMDR,
       GatePC, keyboard_1_avail, LD_CC, LD_IR, LD_MAR, LD_MDR, LD_OFF, LD_OR, LD_PC, LD_PRINT, LD_READ,
       LD_REG, MARMUX, MEM_EN, MEM_HDD, MEM_RW, MIO_EN, not_2_out, or_2_out, POWER, reset, SkipHDD,
       SkipHDD_out, SR2MUX, STOP, WAIT;
  wire [1:0] ADDR2MUX, ALUK, PCMUX;
  wire [2:0] CC_q, DR, logic_1_p, SR1, SR2;
  wire [3:0] PC_q, PC_q_2, PC_q_3, PC_q_4;
  wire [6:0] KEY, transistor_1_out;
  wire [15:0] add_1_out_3, adder_1_out, alu_1_out_4, bit_extender_1_out, bit_extender_2_out,
       bit_extender_3_out, bit_extender_4_out, bit_extender_5_out, bit_extender_6_out, IR, mainOFF, MDR_q,
       mux2_1_out_4, mux2_2_out_4, mux2_3_out_4, mux2_4_out_4, mux4_1_out_6, mux4_2_out_6, n1_1_out_2, OR_q,
       pull_resistor_1_node, reg_file_1_out_8, reg_file_1_out_9, reg_file_1_out_10, reg_file_1_out_11,
       reg_file_1_out_12, reg_file_1_out_13, reg_file_1_out_14, reg_file_1_out_15, reg_file_1_sr1_2,
       reg_file_1_sr2_2, register_1_q, transistor_3_out, transistor_4_out;

  Register #(.width(16)) OR (.D(pull_resistor_1_node), .en(LD_OR), .Q(OR_q), .clk(Clock), .clr(reset));
  // Probe on pull_resistor_1_node
  Transistor #(.gate("br"), .width(7)) transistor_1 (.in(OR_q[6:0]), .out(transistor_1_out), .gate(IR[7]));
  Transistor #(.\type ("n"), .width(7)) transistor_2 (.in(IR[6:0]), .out(transistor_1_out), .gate(IR[7]));
  LED led_1 (.in(POWER));
  Button u_POWER (.out(STOP));
  Pull_Resistor pull_resistor_1 (.node(pull_resistor_1_node));
  Gate gate_1 (.LD(GateMARMUX), .Data(mux2_1_out_4), .Out(pull_resistor_1_node));
  MUX2 mux2_1 (._0(bit_extender_1_out), ._1(add_1_out_3), .in_2(MARMUX), .out_4(mux2_1_out_4));
  assign bit_extender_1_out = {{10{IR[5]}}, IR[5:0]};  // Bit_Extender bit_extender_1
  // Probe on mux4_1_out_6
  MUX4 mux4_1 (
    .in_1(ADDR2MUX), ._3(bit_extender_2_out), ._2(bit_extender_3_out), ._1(bit_extender_4_out),
    ._0({16{1'b0}}), .out_6(mux4_1_out_6));
  assign bit_extender_2_out = {{10{IR[5]}}, IR[5:0]};  // Bit_Extender bit_extender_2
  assign bit_extender_3_out = {{10{IR[5]}}, IR[5:0]};  // Bit_Extender bit_extender_3
  assign bit_extender_4_out = {{10{IR[5]}}, IR[5:0]};  // Bit_Extender bit_extender_4
  // Probe on transistor_1_out
  BitStore bitstore_1 (.Clock(STOP), ._1(1'b1), .LD(1'b1), .Current(POWER));  // open: LD_Next, clear
  Register #(.width(16)) u_IR (.D(pull_resistor_1_node), .en(LD_IR), .Q(IR), .clk(Clock), .clr(reset));
  LOGIC logic_1 (.in_1(pull_resistor_1_node), .N(logic_1_p[2]), .Z(logic_1_p[1]), .P(logic_1_p[0]));
  TTY #(.rows(10)) tty_1 (.data(transistor_1_out), .clk(Clock), .we(LD_PRINT), .clr(reset));
  not not_1 (reset, POWER);
  ADD add_1 (.in_1(mux4_1_out_6), .in_2(mux2_2_out_4), .out_3(add_1_out_3));
  MUX2 mux2_2 (._0({PC_q_4, PC_q_3, PC_q_2, PC_q}), ._1(reg_file_1_sr1_2), .in_2(ADDR1MUX), .out_4(mux2_2_out_4));
  Pull_Resistor pull_resistor_2 (.node(WAIT));
  Register #(.width(3)) CC (.D(logic_1_p), .en(LD_CC), .Q(CC_q), .clk(Clock), .clr(reset));
  Register #(.width(16)) register_1 (.D(pull_resistor_1_node), .en(LD_MAR), .Q(register_1_q), .clk(Clock), .clr(reset));
  DotMatrix #(.matrixcols(4), .matrixrows(4)) dotmatrix_1 (.col0(PC_q_4), .col1(PC_q_3), .col2(PC_q_2), .col3(PC_q));
  // Probe on add_1_out_3
  FSM fsm_1 (
    .R(POWER), .IRin(IR), .DR(DR), .LD_REG(LD_REG), .SR1(SR1), .SR2(SR2), .ALUK(ALUK), .SR2MUX(SR2MUX),
    .LD_CC(LD_CC), .LD_IR(LD_IR), .LD_MDR(LD_MDR), .LD_MAR(LD_MAR), .MIO_EN(MIO_EN), .MEM_EN(MEM_EN),
    .MEM_RW(MEM_RW), .GateMDR(GateMDR), .GateALU(GateALU), .GateMARMUX(GateMARMUX), .GatePC(GatePC),
    .LD_PC(LD_PC), .PCMUX(PCMUX), .MARMUX(MARMUX), .ADDR2MUX(ADDR2MUX), .ADDR1MUX(ADDR1MUX), .Clock(Clock),
    .MEM_HDD(MEM_HDD), .NZPin(CC_q), .GateHDD(GateHDD), .LD_PRINT(LD_PRINT), .LD_READ(LD_READ),
    .LD_OR(LD_OR), .GateKR(GateKR), .WAIT(WAIT), .CKEY(CKEY), .ASK(ASK), .mainOFF(LD_OFF), .SkipHDD(SkipHDD));
  Transistor #(.\type ("n"), .width(16)) transistor_3 (.in(register_1_q), .out(transistor_3_out), .gate(MEM_HDD));
  // Probe on mux4_2_out_6
  MUX4 mux4_2 (
    .in_1(PCMUX), ._3(mainOFF), ._2(pull_resistor_1_node), ._1(add_1_out_3), ._0(n1_1_out_2),
    .out_6(mux4_2_out_6));
  assign bit_extender_5_out = {{11{IR[4]}}, IR[4:0]};  // Bit_Extender bit_extender_5
  LED led_2 (.in(ASK));
  Register #(.width(16)) PC (
    .D(mux4_2_out_6), .en(LD_PC), .Q({PC_q_4, PC_q_3, PC_q_2, PC_q}), .clk(Clock), .clr(reset));
  and and_1 (and_1_out, MEM_RW, ~MEM_HDD);  // AND_Gate
  not not_2 (not_2_out, MEM_RW);
  Gate gate_2 (.LD(GatePC), .Data({PC_q_4, PC_q_3, PC_q_2, PC_q}), .Out(pull_resistor_1_node));
  _1 u_1_1 (.in_1({PC_q_4, PC_q_3, PC_q_2, PC_q}), .out_2(n1_1_out_2));
  Transistor #(.\type ("n"), .width(16)) transistor_4 (.in(MDR_q), .out(transistor_4_out), .gate(and_1_out));
  RAM #(.addrWidth(16), .dataWidth(16)) ram_1 (
    .addr(register_1_q), .data(transistor_4_out), .sel(MEM_EN), .clk(Clock), .ld(not_2_out), .clr(and_2_out));
  and and_2 (and_2_out, reset, ~SkipHDD);  // AND_Gate
  ROM #(.addrWidth(16), .dataWidth(16)) rom_1 (.addr(transistor_3_out), .data(transistor_4_out), .sel(MEM_HDD));
  // Probe on PCMUX
  // Probe on DR
  // Probe on SR2
  MUX2 mux2_3 (._0(reg_file_1_sr2_2), ._1(bit_extender_5_out), .in_2(SR2MUX), .out_4(mux2_3_out_4));
  // Probe on ALUK
  Gate gate_3 (.LD(GateMDR), .Data(MDR_q), .Out(pull_resistor_1_node));
  Register #(.width(16)) MDR (.D(mux2_4_out_4), .en(LD_MDR), .Q(MDR_q), .clk(Clock), .clr(reset));
  MUX2 mux2_4 (._0(transistor_4_out), ._1(pull_resistor_1_node), .in_2(MIO_EN), .out_4(mux2_4_out_4));
  // Probe on pull_resistor_1_node
  REG_FILE reg_file_1 (
    .\input (pull_resistor_1_node), .DR(DR), .LD_REG(LD_REG), .Clock(Clock), .SR2(SR2), .SR1(SR1),
    .SR2_2(reg_file_1_sr2_2), .SR1_2(reg_file_1_sr1_2), .reset(reset), .out_8(reg_file_1_out_8),
    .out_9(reg_file_1_out_9), .out_10(reg_file_1_out_10), .out_11(reg_file_1_out_11),
    .out_12(reg_file_1_out_12), .out_13(reg_file_1_out_13), .out_14(reg_file_1_out_14),
    .out_15(reg_file_1_out_15));
  // Probe on reg_file_1_sr1_2
  ALU alu_1 (.SR1(reg_file_1_sr1_2), .in_2(mux2_3_out_4), .ALUK(ALUK), .out_4(alu_1_out_4));
  Gate gate_4 (.LD(GateALU), .Data(alu_1_out_4), .Out(pull_resistor_1_node));
  Adder #(.width(16)) adder_1 (.a(transistor_4_out), .b(16'h1), .out(adder_1_out));  // open: cin, cout
  Keyboard keyboard_1 (.clk(Clock), .re(LD_READ), .clr(or_2_out), .avail(keyboard_1_avail), .data(KEY));
  // Probe on SR1
  Gate gate_5 (.LD(GateHDD), .Data(transistor_4_out), .Out(pull_resistor_1_node));
  Multiplexer #(.width(16)) multiplexer_1 (
    .in0({16{1'b0}}), .in1(adder_1_out), .out(mainOFF), .sel(LD_OFF), .en(LD_OFF));
  Button u_SkipHDD (.out(SkipHDD_out));
  LED led_3 (.in(SkipHDD));
  or or_2 (or_2_out, CKEY, reset);
  // Probe on mux2_4_out_4
  // Probe on transistor_4_out
  Pull_Resistor pull_resistor_3 (.node(mainOFF));
  BitStore bitstore_2 (.Clock(SkipHDD_out), ._1(1'b1), .LD(1'b1), .Current(SkipHDD));  // open: LD_Next, clear
  not not_3 (WAIT, keyboard_1_avail);
  Gate gate_6 (.LD(GateKR), .Data(bit_extender_6_out), .Out(pull_resistor_1_node));
  assign bit_extender_6_out = {{9{1'b0}}, KEY};  // Bit_Extender bit_extender_6
  LED led_4 (.in(LD_REG));
  LED led_5 (.in(LD_CC));
  LED led_6 (.in(LD_IR));
  LED led_7 (.in(LD_MDR));
  LED led_8 (.in(LD_MAR));
  LED led_9 (.in(LD_PC));
  LED led_10 (.in(MEM_RW));
  LED led_11 (.in(MEM_EN));
  LED led_12 (.in(MEM_HDD));
  LED led_13 (.in(GateALU));
  LED led_14 (.in(GateMARMUX));
  LED led_15 (.in(GatePC));
  LED led_16 (.in(GateMDR));
  LED led_17 (.in(GateHDD));
  LED led_18 (.in(Clock));
  // Probe on bit_extender_6_out
  // Probe on reg_file_1_out_8
  // Probe on reg_file_1_out_9
  // Probe on reg_file_1_out_10
  // Probe on reg_file_1_out_11
  // Probe on reg_file_1_out_12
  // Probe on reg_file_1_out_13
  // Probe on reg_file_1_out_14
  // Probe on reg_file_1_out_15

  // Notes on the sheet:
  //   N
  //   ics
  //   I
  //   nternal
  //   C
  //   S
  //   omputer
  //   ystem
  //   contents of rom_1 (hex, n*v repeats v):
  //   11 5*0 30 fff6 49 54 5f 57 4f 52 4b 53 21 0 2bf4 27f2 14aa 14aa 14ac 98ff 1921 8000 1004 8a00 88ab
  //   8a00 8100 1244 8a00 1001 88bd 8a00 1b40 802 88b1 1036 0 1003 8800 13ea 8900 31d3 33d3 8 21fe 6200
  //   1021 8900 bfb 21cb 23cb d000
endmodule

module FSM (
  input  R,
  input  SkipHDD,
  input  WAIT,
  input  [15:0] IRin,
  input  [2:0] NZPin,
  output [2:0] DR,
  output LD_REG,
  output [2:0] SR1,
  output [2:0] SR2,
  output [1:0] ALUK,
  output SR2MUX,
  output LD_CC,
  output LD_IR,
  output LD_MDR,
  output LD_MAR,
  output MIO_EN,
  output MEM_EN,
  output MEM_RW,
  output MEM_HDD,
  output GateMDR,
  output GateALU,
  output GateMARMUX,
  output GatePC,
  output GateHDD,
  output LD_PC,
  output [1:0] PCMUX,
  output MARMUX,
  output [1:0] ADDR2MUX,
  output ADDR1MUX,
  output Clock,
  output LD_PRINT,
  output LD_READ,
  output LD_OR,
  output GateKR,
  output CKEY,
  output ASK,
  output mainOFF
);

  wire ADD, AND, and_1_out, and_8_out, and_17_out, and_19_out, and_20_out, and_21_out, and_24_out,
       and_25_out, and_26_out, and_27_out, and_28_out, and_29_out, and_30_out, and_31_out, and_32_out,
       and_33_out, and_34_out, and_35_out, bitstore_1_current, bitstore_2_ld_next, bitstore_3_current,
       bitstore_3_ld_next, BR, buffer2b_1_out, buffer2b_3_out, buffer2b_4_out, buffer2b_5_out,
       buffer2b_6_out, buffer2b_7_out, buffer2b_8_out, buffer2b_9_out, buffer2b_10_out, buffer2b_11_out,
       buffer2b_15_out, buffer2b_16_out, buffer3b_1_out, buffer3b_6_out, buffer3b_7_out, buffer3b_8_out,
       buffer3b_10_out, buffer3b_12_out, buffer3b_13_out, buffer3b_15_out, buffer_1_out, buffer_2_out,
       buffer_3_out, buffer_5_out, buffer_7_out, buffer_8_out, buffer_9_out, buffer_10_out, buffer_11_out,
       buffer_12_out, buffer_13_out, buffer_14_out, buffer_15_out, buffer_16_out, buffer_17_out,
       buffer_18_out, buffer_19_out, buffer_20_out, buffer_21_out, buffer_22_out, buffer_23_out,
       buffer_24_out, buffer_25_out, buffer_26_out, buffer_27_out, buffer_28_out, buffer_29_out,
       buffer_30_out, buffer_31_out, buffer_32_out, buffer_33_out, buffer_34_out, buffer_35_out,
       buffer_36_out, buffer_37_out, buffer_38_out, buffer_39_out, buffer_40_out, buffer_41_out,
       buffer_42_out, buffer_43_out, buffer_44_out, buffer_45_out, buffer_46_out, buffer_49_out,
       buffer_50_out, buffer_52_out, buffer_53_out, buffer_55_out, buffer_56_out, buffer_57_out,
       buffer_58_out, buffer_59_out, buffer_60_out, buffer_61_out, buffer_63_out, buffer_64_out,
       buffer_65_out, buffer_66_out, buffer_67_out, buffer_68_out, buffer_69_out, buffer_70_out,
       buffer_72_out, buffer_73_out, buffer_74_out, buffer_75_out, buffer_76_out, buffer_77_out,
       buffer_79_out, buffer_82_out, buffer_83_out, buffer_85_out, buffer_86_out, buffer_92_out,
       buffer_93_out, buffer_94_out, buffer_95_out, buffer_96_out, buffer_97_out, buffer_98_out,
       buffer_99_out, buffer_100_out, buffer_101_out, buffer_102_out, buffer_104_out, buffer_105_out,
       buffer_106_out, buffer_107_out, buffer_108_out, buffer_109_out, buffer_110_out, buffer_111_out,
       buffer_112_out, buffer_113_out, buffer_114_out, buffer_115_out, buffer_116_out, buffer_117_out,
       buffer_119_out, buffer_120_out, clear, clock_1_out, command_1_on_2, command_1_select_line,
       command_2_on_2, command_2_select_line, command_3_on_2, command_3_select_line, command_4_on_2,
       command_4_select_line, command_5_on_2, command_5_select_line, command_6_on_2, command_6_select_line,
       command_7_on_2, command_7_select_line, command_8_on_2, command_8_select_line, command_9_on_2,
       command_9_select_line, command_10_on_2, command_10_select_line, command_11_on_2,
       command_11_select_line, command_12_on_2, command_12_select_line, command_13_on_2,
       command_13_select_line, command_14_on_2, command_15_on_2, command_15_select_line, command_16_on_2,
       command_16_select_line, command_17_on_2, command_17_select_line, command_18_on_2,
       command_18_select_line, command_19_on_2, command_19_select_line, command_20_on_2,
       command_20_select_line, command_21_on_2, command_21_select_line, command_22_on_2,
       command_22_select_line, command_23_on_2, command_23_select_line, command_24_on_2,
       command_24_select_line, command_25_on_2, command_25_select_line, command_26_on_2,
       command_26_select_line, command_27_on_2, command_27_select_line, command_28_on_2,
       command_28_select_line, command_29_on_2, command_29_select_line, command_30_on_2,
       command_30_select_line, command_31_on_2, command_31_select_line, command_32_on_2,
       command_32_select_line, command_33_on_2, command_33_select_line, command_34_on_2,
       command_34_select_line, command_35_on_2, command_35_select_line, command_36_on_2,
       command_36_select_line, command_37_on_2, command_37_select_line, command_38_on_2,
       command_38_select_line, command_39_on_2, command_39_select_line, command_40_on_2,
       command_40_select_line, command_41_on_2, command_41_select_line, command_42_on_2,
       command_42_select_line, command_43_on_2, command_43_select_line, command_44_on_2,
       command_44_select_line, command_45_on_2, command_45_select_line, command_46_on_2,
       command_46_select_line, command_47_on_2, command_47_select_line, command_48_on_2,
       command_48_select_line, command_49_select_line, CycleEnd, ENFORCED_STOP, HDDcheck, JMP, JSR, LD, LDI,
       LDR, LEA, NOT, or_1_out, or_2_out, or_3_out, or_4_out, or_5_out, or_6_out, or_7_out, or_8_out,
       or_9_out, or_10_out, or_11_out, PRINT, PRINTC, READ, ReadHDD, ReadMEM, ST, STI, STR, ToggleHDD, TRAP;

  not not_1 (clear, R);
  and and_1 (and_1_out, R, ~CycleEnd);  // AND_Gate
  // XOR_Gate xor_1 has open pins: in0=CycleEnd, in1=bitstore_3_ld_next, out=open
  Command command_1 (
    .Select_Line(command_1_select_line), .On(command_5_on_2), .Clock(Clock), .Start(command_5_select_line),
    .On_2(command_1_on_2), .CommandON(ToggleHDD));  // open: in_5
  Command command_2 (
    .Select_Line(command_2_select_line), .On(command_1_on_2), .Clock(Clock), .Start(command_1_select_line),
    .On_2(command_2_on_2), .CommandON(ToggleHDD));  // open: in_5
  Command command_3 (
    .Select_Line(command_3_select_line), .On(command_2_on_2), .Clock(Clock), .Start(command_2_select_line),
    .On_2(command_3_on_2), .CommandON(ToggleHDD));  // open: in_5
  BitStore bitstore_1 (
    .Clock(Clock), ._1(and_1_out), .LD(and_1_out), .Current(bitstore_1_current), .clear(clear));  // open: LD_Next
  BitStore bitstore_2 (
    .Clock(Clock), ._1(command_1_select_line), .LD(command_1_select_line), .Current(ReadMEM),
    .LD_Next(bitstore_2_ld_next), .clear(clear));
  Buffer buffer_1 (.in(command_2_select_line), .out(buffer_1_out), .out_2(GatePC));
  Buffer buffer_2 (.in(command_3_select_line), .out(buffer_2_out), .out_2(mainOFF));
  and and_2 (TRAP, IRin[15], IRin[14], IRin[13], IRin[12]);
  and and_3 (LEA, IRin[15], IRin[14], IRin[13], ~IRin[12]);  // AND_Gate
  and and_4 (ToggleHDD, IRin[15], IRin[14], ~IRin[13], IRin[12]);  // AND_Gate
  and RET_JMP (JMP, IRin[15], IRin[14], ~IRin[13], ~IRin[12]);  // AND_Gate
  and and_5 (STI, IRin[15], ~IRin[14], IRin[13], IRin[12]);  // AND_Gate
  and and_6 (LDI, IRin[15], ~IRin[14], IRin[13], ~IRin[12]);  // AND_Gate
  and and_7 (NOT, IRin[15], ~IRin[14], ~IRin[13], IRin[12]);  // AND_Gate
  and and_8 (and_8_out, IRin[15], ~IRin[14], ~IRin[13], ~IRin[12]);  // AND_Gate
  and and_9 (STR, ~IRin[15], IRin[14], IRin[13], IRin[12]);  // AND_Gate
  and and_10 (LDR, ~IRin[15], IRin[14], IRin[13], ~IRin[12]);  // AND_Gate
  and and_11 (AND, ~IRin[15], IRin[14], ~IRin[13], IRin[12]);  // AND_Gate
  and and_12 (JSR, ~IRin[15], IRin[14], ~IRin[13], ~IRin[12]);  // AND_Gate
  and and_13 (ST, ~IRin[15], ~IRin[14], IRin[13], IRin[12]);  // AND_Gate
  and and_14 (LD, ~IRin[15], ~IRin[14], IRin[13], ~IRin[12]);  // AND_Gate
  and and_15 (ADD, ~IRin[15], ~IRin[14], ~IRin[13], IRin[12]);  // AND_Gate
  and and_16 (BR, ~IRin[15], ~IRin[14], ~IRin[13], ~IRin[12]);  // AND_Gate
  not not_2 (ReadHDD, bitstore_2_ld_next);
  Buffer buffer_3 (.in(command_1_select_line), .out(buffer_3_out), .out_2(LD_PC));
  Buffer buffer_4 (.in(buffer_1_out), .out_2(LD_MAR));  // open: out
  Buffer buffer_5 (.in(buffer_2_out), .out(buffer_5_out), .out_2(MEM_EN));
  Buffer2b buffer2b_1 (.Value(2'b11), .in(buffer_5_out), .out(buffer2b_1_out), .out_3(PCMUX));
  and and_17 (and_17_out, and_8_out, IRin[11]);
  and and_18 (READ, and_8_out, ~IRin[11]);  // AND_Gate
  Buffer2b buffer2b_2 (.Value(2'b11), .in(buffer_3_out), .out_3(PCMUX));  // open: out
  Buffer buffer_6 (.in(buffer2b_1_out), .out_2(LD_PC));  // open: out
  and and_19 (and_19_out, IRin[9], NZPin[0]);
  and and_20 (and_20_out, IRin[10], NZPin[1]);
  and and_21 (and_21_out, IRin[11], NZPin[2]);
  and and_22 (PRINTC, IRin[7], and_17_out);
  and and_23 (PRINT, and_17_out, ~IRin[7]);  // AND_Gate
  or or_1 (or_1_out, bitstore_1_current, bitstore_3_ld_next);
  or or_2 (or_2_out, and_25_out, and_32_out, command_3_on_2);
  BitStore bitstore_3 (
    .Clock(Clock), ._1(or_1_out), .LD(or_1_out), .Current(bitstore_3_current), .LD_Next(bitstore_3_ld_next));  // open: clear
  and and_24 (and_24_out, bitstore_3_ld_next, ReadHDD);
  Command command_4 (
    .Select_Line(command_4_select_line), .On(and_24_out), .Clock(Clock), .Start(and_31_out),
    .On_2(command_4_on_2), .CommandON(ReadHDD));  // open: in_5
  Command command_5 (
    .Select_Line(command_5_select_line), .On(command_4_on_2), .Clock(Clock), .Start(command_4_select_line),
    .On_2(command_5_on_2), .CommandON(ReadHDD));  // open: in_5
  and and_25 (and_25_out, bitstore_3_ld_next, ~and_24_out);  // AND_Gate
  or or_3 (or_3_out, and_26_out, and_32_out, command_5_select_line);
  Command command_6 (
    .Select_Line(command_6_select_line), .On(or_2_out), .Clock(Clock), .Start(or_3_out),
    .On_2(command_6_on_2), .CommandON(or_4_out));  // open: in_5
  or or_4 (or_4_out, ReadMEM, SkipHDD);
  Command command_7 (
    .Select_Line(command_7_select_line), .On(command_6_on_2), .Clock(Clock), .Start(command_6_select_line),
    .On_2(command_7_on_2), .CommandON(or_5_out));  // open: in_5
  or or_5 (or_5_out, ReadMEM, SkipHDD);
  Command command_8 (
    .Select_Line(command_8_select_line), .On(command_7_on_2), .Clock(Clock), .Start(command_7_select_line),
    .On_2(command_8_on_2), .CommandON(or_6_out));  // open: in_5
  or or_6 (or_6_out, ReadMEM, SkipHDD);
  Command command_9 (
    .Select_Line(command_9_select_line), .On(command_8_on_2), .Clock(Clock), .Start(command_8_select_line),
    .On_2(command_9_on_2), .CommandON(AND));  // open: in_5
  Command command_10 (
    .Select_Line(command_10_select_line), .On(command_9_on_2), .Clock(Clock), .Start(command_8_select_line),
    .On_2(command_10_on_2), .CommandON(BR));  // open: in_5
  Command command_11 (
    .Select_Line(command_11_select_line), .On(command_10_on_2), .Clock(Clock), .Start(command_8_select_line),
    .On_2(command_11_on_2), .CommandON(JMP));  // open: in_5
  Command command_12 (
    .Select_Line(command_12_select_line), .On(command_11_on_2), .Clock(Clock), .Start(command_8_select_line),
    .On_2(command_12_on_2), .CommandON(JSR));  // open: in_5
  Command command_13 (
    .Select_Line(command_13_select_line), .On(command_12_on_2), .Clock(Clock), .Start(command_8_select_line),
    .On_2(command_13_on_2), .CommandON(NOT));  // open: in_5
  Command command_14 (
    .Select_Line(ENFORCED_STOP), .On(command_13_on_2), .Clock(Clock), .Start(command_8_select_line),
    .On_2(command_14_on_2), .CommandON(ToggleHDD), .in_5(clear));
  Command command_15 (
    .Select_Line(command_15_select_line), .On(command_14_on_2), .Clock(Clock), .Start(command_8_select_line),
    .On_2(command_15_on_2), .CommandON(LD));  // open: in_5
  Command command_16 (
    .Select_Line(command_16_select_line), .On(command_15_on_2), .Clock(Clock),
    .Start(command_15_select_line), .On_2(command_16_on_2), .CommandON(LD));  // open: in_5
  Command command_17 (
    .Select_Line(command_17_select_line), .On(command_16_on_2), .Clock(Clock),
    .Start(command_16_select_line), .On_2(command_17_on_2), .CommandON(LD));  // open: in_5
  Command command_18 (
    .Select_Line(command_18_select_line), .On(command_17_on_2), .Clock(Clock), .Start(command_8_select_line),
    .On_2(command_18_on_2), .CommandON(LDI));  // open: in_5
  Command command_19 (
    .Select_Line(command_19_select_line), .On(command_18_on_2), .Clock(Clock),
    .Start(command_18_select_line), .On_2(command_19_on_2), .CommandON(LDI));  // open: in_5
  Command command_20 (
    .Select_Line(command_20_select_line), .On(command_19_on_2), .Clock(Clock),
    .Start(command_19_select_line), .On_2(command_20_on_2), .CommandON(LDI));  // open: in_5
  Command command_21 (
    .Select_Line(command_21_select_line), .On(command_20_on_2), .Clock(Clock),
    .Start(command_20_select_line), .On_2(command_21_on_2), .CommandON(LDI));  // open: in_5
  Command command_22 (
    .Select_Line(command_22_select_line), .On(command_21_on_2), .Clock(Clock),
    .Start(command_21_select_line), .On_2(command_22_on_2), .CommandON(LDI));  // open: in_5
  Command command_23 (
    .Select_Line(command_23_select_line), .On(command_22_on_2), .Clock(Clock), .Start(command_8_select_line),
    .On_2(command_23_on_2), .CommandON(LDR));  // open: in_5
  Command command_24 (
    .Select_Line(command_24_select_line), .On(command_23_on_2), .Clock(Clock),
    .Start(command_23_select_line), .On_2(command_24_on_2), .CommandON(LDR));  // open: in_5
  Command command_25 (
    .Select_Line(command_25_select_line), .On(command_24_on_2), .Clock(Clock),
    .Start(command_24_select_line), .On_2(command_25_on_2), .CommandON(LDR));  // open: in_5
  Command command_26 (
    .Select_Line(command_26_select_line), .On(command_25_on_2), .Clock(Clock), .Start(command_8_select_line),
    .On_2(command_26_on_2), .CommandON(LEA));  // open: in_5
  Command command_27 (
    .Select_Line(command_27_select_line), .On(command_26_on_2), .Clock(Clock), .Start(command_8_select_line),
    .On_2(command_27_on_2), .CommandON(ST));  // open: in_5
  Command command_28 (
    .Select_Line(command_28_select_line), .On(command_27_on_2), .Clock(Clock),
    .Start(command_27_select_line), .On_2(command_28_on_2), .CommandON(ST));  // open: in_5
  Command command_29 (
    .Select_Line(command_29_select_line), .On(command_28_on_2), .Clock(Clock),
    .Start(command_28_select_line), .On_2(command_29_on_2), .CommandON(ST));  // open: in_5
  Command command_30 (
    .Select_Line(command_30_select_line), .On(command_29_on_2), .Clock(Clock), .Start(command_8_select_line),
    .On_2(command_30_on_2), .CommandON(STI));  // open: in_5
  Command command_31 (
    .Select_Line(command_31_select_line), .On(command_30_on_2), .Clock(Clock),
    .Start(command_30_select_line), .On_2(command_31_on_2), .CommandON(STI));  // open: in_5
  Command command_32 (
    .Select_Line(command_32_select_line), .On(command_31_on_2), .Clock(Clock),
    .Start(command_31_select_line), .On_2(command_32_on_2), .CommandON(STI));  // open: in_5
  Command command_33 (
    .Select_Line(command_33_select_line), .On(command_32_on_2), .Clock(Clock),
    .Start(command_32_select_line), .On_2(command_33_on_2), .CommandON(STI));  // open: in_5
  Command command_34 (
    .Select_Line(command_34_select_line), .On(command_33_on_2), .Clock(Clock),
    .Start(command_33_select_line), .On_2(command_34_on_2), .CommandON(STI));  // open: in_5
  Command command_35 (
    .Select_Line(command_35_select_line), .On(command_34_on_2), .Clock(Clock), .Start(command_8_select_line),
    .On_2(command_35_on_2), .CommandON(STR));  // open: in_5
  Command command_36 (
    .Select_Line(command_36_select_line), .On(command_35_on_2), .Clock(Clock),
    .Start(command_35_select_line), .On_2(command_36_on_2), .CommandON(STR));  // open: in_5
  Command command_37 (
    .Select_Line(command_37_select_line), .On(command_36_on_2), .Clock(Clock),
    .Start(command_36_select_line), .On_2(command_37_on_2), .CommandON(STR));  // open: in_5
  Command command_38 (
    .Select_Line(command_38_select_line), .On(command_37_on_2), .Clock(Clock), .On_2(command_38_on_2),
    .CommandON(TRAP));  // open: Start, in_5
  Command command_39 (
    .Select_Line(command_39_select_line), .On(command_38_on_2), .Clock(Clock),
    .Start(command_38_select_line), .On_2(command_39_on_2), .CommandON(TRAP));  // open: in_5
  Command command_40 (
    .Select_Line(command_40_select_line), .On(command_39_on_2), .Clock(Clock),
    .Start(command_39_select_line), .On_2(command_40_on_2), .CommandON(TRAP));  // open: in_5
  Command command_41 (
    .Select_Line(command_41_select_line), .On(command_40_on_2), .Clock(Clock), .Start(command_8_select_line),
    .On_2(command_41_on_2), .CommandON(PRINT));  // open: in_5
  Command command_42 (
    .Select_Line(command_42_select_line), .On(command_41_on_2), .Clock(Clock),
    .Start(command_41_select_line), .On_2(command_42_on_2), .CommandON(PRINT));  // open: in_5
  Command command_43 (
    .Select_Line(command_43_select_line), .On(command_42_on_2), .Clock(Clock), .Start(command_8_select_line),
    .On_2(command_43_on_2), .CommandON(PRINTC));  // open: in_5
  Command command_44 (
    .Select_Line(command_44_select_line), .On(command_43_on_2), .Clock(Clock), .Start(command_8_select_line),
    .On_2(command_44_on_2), .CommandON(READ));  // open: in_5
  or or_7 (or_7_out, buffer_49_out, and_29_out);
  or or_8 (or_8_out, and_29_out, command_44_on_2);
  Command command_45 (
    .Select_Line(command_45_select_line), .On(or_8_out), .Clock(Clock), .Start(or_7_out),
    .On_2(command_45_on_2), .CommandON(READ));  // open: in_5
  Command command_46 (
    .Select_Line(command_46_select_line), .On(and_27_out), .Clock(Clock), .Start(and_27_out),
    .On_2(command_46_on_2), .CommandON(READ));  // open: in_5
  or or_9 (or_9_out, and_30_out, and_28_out);
  or or_10 (or_10_out, and_28_out, command_45_on_2, command_46_on_2);
  Command command_47 (
    .Select_Line(command_47_select_line), .On(or_10_out), .Clock(Clock), .Start(or_9_out),
    .On_2(command_47_on_2), .CommandON(READ));  // open: in_5
  Command command_48 (
    .Select_Line(command_48_select_line), .On(command_47_on_2), .Clock(Clock),
    .Start(command_47_select_line), .On_2(command_48_on_2), .CommandON(READ));  // open: in_5
  Command command_49 (
    .Select_Line(command_49_select_line), .On(command_48_on_2), .Clock(Clock), .Start(command_8_select_line),
    .On_2(CycleEnd), .CommandON(ADD));  // open: in_5
  Buffer buffer_7 (.in(command_4_select_line), .out(buffer_7_out), .out_2(LD_PC));
  Buffer buffer_8 (.in(command_5_select_line), .out(buffer_8_out), .out_2(LD_MDR));
  and and_26 (and_26_out, ~command_5_select_line, bitstore_3_ld_next);  // AND_Gate
  Buffer buffer_9 (.in(command_6_select_line), .out(buffer_9_out), .out_2(LD_PC));
  Buffer buffer_10 (.in(buffer_9_out), .out(buffer_10_out), .out_2(LD_MAR));
  Buffer buffer_11 (.in(command_7_select_line), .out(buffer_11_out), .out_2(LD_MDR));
  Buffer buffer_12 (.in(buffer_11_out), .out(buffer_12_out), .out_2(MEM_EN));
  Buffer buffer_13 (.in(command_8_select_line), .out(buffer_13_out), .out_2(GateMDR));
  Buffer buffer_14 (.in(buffer_13_out), .out(buffer_14_out), .out_2(LD_IR));
  Buffer buffer_15 (.in(command_9_select_line), .out(buffer_15_out), .out_2(GateALU));
  or or_11 (or_11_out, and_19_out, and_20_out, and_21_out);
  Buffer buffer_16 (.in(command_11_select_line), .out(buffer_16_out), .out_2(LD_PC));
  Buffer buffer_17 (.in(command_12_select_line), .out(buffer_17_out), .out_2(LD_PC));
  Buffer buffer_18 (.in(buffer_19_out), .out(buffer_18_out), .out_2(LD_CC));
  Buffer buffer_19 (.in(command_13_select_line), .out(buffer_19_out), .out_2(LD_REG));
  Buffer buffer_20 (.in(command_15_select_line), .out(buffer_20_out), .out_2(LD_MAR));
  Buffer buffer_21 (.in(command_16_select_line), .out(buffer_21_out), .out_2(LD_MDR));
  Buffer buffer_22 (.in(command_17_select_line), .out(buffer_22_out), .out_2(LD_REG));
  Buffer buffer_23 (.in(command_18_select_line), .out(buffer_23_out), .out_2(LD_MAR));
  Buffer buffer_24 (.in(command_19_select_line), .out(buffer_24_out), .out_2(LD_MDR));
  Buffer buffer_25 (.in(command_20_select_line), .out(buffer_25_out), .out_2(LD_MAR));
  Buffer buffer_26 (.in(command_21_select_line), .out(buffer_26_out), .out_2(LD_MDR));
  Buffer buffer_27 (.in(command_22_select_line), .out(buffer_27_out), .out_2(LD_CC));
  Buffer buffer_28 (.in(command_23_select_line), .out(buffer_28_out), .out_2(LD_MAR));
  Buffer buffer_29 (.in(command_24_select_line), .out(buffer_29_out), .out_2(LD_MDR));
  Buffer buffer_30 (.in(command_25_select_line), .out(buffer_30_out), .out_2(LD_CC));
  Buffer buffer_31 (.in(command_26_select_line), .out(buffer_31_out), .out_2(LD_CC));
  Buffer buffer_32 (.in(command_27_select_line), .out(buffer_32_out), .out_2(GateMARMUX));
  Buffer buffer_33 (.in(command_28_select_line), .out(buffer_33_out), .out_2(LD_MDR));
  Buffer buffer_34 (.in(command_29_select_line), .out(buffer_34_out), .out_2(MEM_EN));
  Buffer buffer_35 (.in(command_30_select_line), .out(buffer_35_out), .out_2(LD_MAR));
  Buffer buffer_36 (.in(command_31_select_line), .out(buffer_36_out), .out_2(MEM_EN));
  Buffer buffer_37 (.in(command_32_select_line), .out(buffer_37_out), .out_2(LD_MAR));
  Buffer buffer_38 (.in(command_33_select_line), .out(buffer_38_out), .out_2(LD_MDR));
  Buffer buffer_39 (.in(command_34_select_line), .out(buffer_39_out), .out_2(MEM_EN));
  Buffer buffer_40 (.in(command_35_select_line), .out(buffer_40_out), .out_2(LD_MDR));
  Buffer buffer_41 (.in(command_36_select_line), .out(buffer_41_out), .out_2(LD_MDR));
  Buffer buffer_42 (.in(command_37_select_line), .out(buffer_42_out), .out_2(MEM_EN));
  Buffer buffer_43 (.in(command_38_select_line), .out(buffer_43_out), .out_2(LD_MDR));
  Buffer buffer_44 (.in(command_39_select_line), .out(buffer_44_out), .out_2(LD_MDR));
  Buffer buffer_45 (.in(command_40_select_line), .out(buffer_45_out), .out_2(LD_PC));
  Buffer3b buffer3b_1 (.Value(IRin[10:8]), .in(command_41_select_line), .out(buffer3b_1_out), .out_3(SR1));
  Buffer buffer_46 (.in(buffer3b_1_out), .out(buffer_46_out), .out_2(GateALU));
  Buffer buffer_47 (.in(command_42_select_line), .out_2(LD_PRINT));  // open: out
  Buffer buffer_48 (.in(command_43_select_line), .out_2(LD_PRINT));  // open: out
  Buffer buffer_49 (.in(command_44_select_line), .out(buffer_49_out), .out_2(CKEY));
  and and_27 (and_27_out, WAIT, command_45_select_line);
  and and_28 (and_28_out, command_45_select_line, ~WAIT);  // AND_Gate
  and and_29 (and_29_out, WAIT, command_46_select_line);
  and and_30 (and_30_out, command_46_select_line, ~WAIT);  // AND_Gate
  Buffer buffer_50 (.in(command_47_select_line), .out(buffer_50_out), .out_2(LD_READ));
  Buffer buffer_51 (.in(command_48_select_line), .out_2(LD_PRINT));  // open: out
  Buffer buffer_52 (.in(command_49_select_line), .out(buffer_52_out), .out_2(GateALU));
  and and_31 (and_31_out, ~SkipHDD, bitstore_3_current);  // AND_Gate
  and and_32 (and_32_out, bitstore_3_current, SkipHDD);
  Buffer buffer_53 (.in(buffer_7_out), .out(buffer_53_out), .out_2(LD_MAR));
  Buffer buffer_54 (.in(buffer_53_out), .out_2(GatePC));  // open: out
  Buffer buffer_55 (.in(buffer_8_out), .out(buffer_55_out), .out_2(MEM_RW));
  Buffer buffer_56 (.in(buffer_55_out), .out(buffer_56_out), .out_2(MEM_EN));
  Buffer buffer_57 (.in(buffer_10_out), .out(buffer_57_out), .out_2(GatePC));
  Buffer buffer_58 (.in(buffer_59_out), .out(buffer_58_out), .out_2(LD_CC));
  Buffer buffer_59 (.in(buffer_15_out), .out(buffer_59_out), .out_2(LD_REG));
  and and_33 (and_33_out, command_10_select_line, or_11_out);
  Buffer2b buffer2b_3 (.Value(2'b10), .in(buffer_16_out), .out(buffer2b_3_out), .out_3(PCMUX));
  Buffer3b buffer3b_2 (.Value(IRin[8:6]), .in(buffer2b_3_out), .out_3(SR1));  // open: out
  Buffer buffer_60 (.in(buffer_17_out), .out(buffer_60_out), .out_2(LD_REG));
  Buffer2b buffer2b_4 (.Value(2'b11), .in(buffer_18_out), .out(buffer2b_4_out), .out_3(ALUK));
  Buffer buffer_61 (.in(buffer_20_out), .out(buffer_61_out), .out_2(GateMARMUX));
  Buffer buffer_62 (.in(buffer_21_out), .out_2(MEM_EN));  // open: out
  Buffer buffer_63 (.in(buffer_22_out), .out(buffer_63_out), .out_2(GateMDR));
  Buffer buffer_64 (.in(buffer_23_out), .out(buffer_64_out), .out_2(GateMARMUX));
  Buffer buffer_65 (.in(buffer_24_out), .out(buffer_65_out), .out_2(MEM_EN));
  Buffer buffer_66 (.in(buffer_25_out), .out(buffer_66_out), .out_2(GateMDR));
  Buffer buffer_67 (.in(buffer_26_out), .out(buffer_67_out), .out_2(MEM_EN));
  Buffer buffer_68 (.in(buffer_69_out), .out(buffer_68_out), .out_2(GateMDR));
  Buffer buffer_69 (.in(buffer_27_out), .out(buffer_69_out), .out_2(LD_REG));
  Buffer buffer_70 (.in(buffer_28_out), .out(buffer_70_out), .out_2(GateMARMUX));
  Buffer buffer_71 (.in(buffer_29_out), .out_2(MEM_EN));  // open: out
  Buffer buffer_72 (.in(buffer_30_out), .out(buffer_72_out), .out_2(LD_REG));
  Buffer buffer_73 (.in(buffer_72_out), .out(buffer_73_out), .out_2(GateMDR));
  Buffer buffer_74 (.in(buffer_31_out), .out(buffer_74_out), .out_2(GateMARMUX));
  Buffer buffer_75 (.in(buffer_32_out), .out(buffer_75_out), .out_2(MARMUX));
  Buffer buffer_76 (.in(buffer_77_out), .out(buffer_76_out), .out_2(GateMARMUX));
  Buffer buffer_77 (.in(buffer_33_out), .out(buffer_77_out), .out_2(MIO_EN));
  Buffer buffer_78 (.in(buffer_34_out), .out_2(MEM_RW));  // open: out
  Buffer buffer_79 (.in(buffer_35_out), .out(buffer_79_out), .out_2(GateMARMUX));
  Buffer buffer_80 (.in(buffer_36_out), .out_2(MEM_RW));  // open: out
  Buffer buffer_81 (.in(buffer_37_out), .out_2(GateMDR));  // open: out
  Buffer buffer_82 (.in(buffer_83_out), .out(buffer_82_out), .out_2(GateMARMUX));
  Buffer buffer_83 (.in(buffer_38_out), .out(buffer_83_out), .out_2(MIO_EN));
  Buffer buffer_84 (.in(buffer_39_out), .out_2(MEM_RW));  // open: out
  Buffer2b buffer2b_5 (.Value(2'b01), .in(buffer_40_out), .out(buffer2b_5_out), .out_3(ADDR2MUX));
  Buffer buffer_85 (.in(buffer_86_out), .out(buffer_85_out), .out_2(GateMARMUX));
  Buffer buffer_86 (.in(buffer_41_out), .out(buffer_86_out), .out_2(MIO_EN));
  Buffer buffer_87 (.in(buffer_42_out), .out_2(MEM_RW));  // open: out
  Buffer buffer_88 (.in(buffer_43_out), .out_2(GateMARMUX));  // open: out
  Buffer buffer_89 (.in(buffer_44_out), .out_2(MEM_EN));  // open: out
  Buffer buffer_90 (.in(buffer2b_6_out), .out_2(GateMDR));  // open: out
  Buffer2b buffer2b_6 (.Value(2'b10), .in(buffer_45_out), .out(buffer2b_6_out), .out_3(PCMUX));
  Buffer buffer_91 (.in(buffer_46_out), .out_2(LD_OR));  // open: out
  Buffer buffer_92 (.in(buffer_50_out), .out(buffer_92_out), .out_2(GateKR));
  Buffer buffer_93 (.in(buffer_94_out), .out(buffer_93_out), .out_2(LD_CC));
  Buffer buffer_94 (.in(buffer_52_out), .out(buffer_94_out), .out_2(LD_REG));
  Buffer buffer_95 (.in(buffer_56_out), .out(buffer_95_out), .out_2(MEM_HDD));
  Buffer2b buffer2b_7 (.Value(2'b10), .in(buffer_58_out), .out(buffer2b_7_out), .out_3(ALUK));
  Buffer buffer_96 (.in(buffer2b_8_out), .out(buffer_96_out), .out_2(LD_PC));
  Buffer2b buffer2b_8 (.Value(2'b10), .in(and_33_out), .out(buffer2b_8_out), .out_3(ADDR2MUX));
  Buffer2b buffer2b_9 (.Value(2'b01), .in(buffer_60_out), .out(buffer2b_9_out), .out_3(PCMUX));
  Buffer buffer_97 (.in(buffer2b_4_out), .out(buffer_97_out), .out_2(GateALU));
  Buffer buffer_98 (.in(buffer_61_out), .out(buffer_98_out), .out_2(MARMUX));
  Buffer3b buffer3b_3 (.Value(IRin[11:9]), .in(buffer_99_out), .out_3(DR));  // open: out
  Buffer buffer_99 (.in(buffer_63_out), .out(buffer_99_out), .out_2(LD_CC));
  Buffer buffer_100 (.in(buffer_64_out), .out(buffer_100_out), .out_2(MARMUX));
  Buffer3b buffer3b_4 (.Value(IRin[11:9]), .in(buffer_68_out), .out_3(DR));  // open: out
  Buffer buffer_101 (.in(buffer_70_out), .out(buffer_101_out), .out_2(MARMUX));
  Buffer3b buffer3b_5 (.Value(IRin[11:9]), .in(buffer_73_out), .out_3(DR));  // open: out
  Buffer buffer_102 (.in(buffer_74_out), .out(buffer_102_out), .out_2(MARMUX));
  Buffer2b buffer2b_10 (.Value(2'b10), .in(buffer_75_out), .out(buffer2b_10_out), .out_3(ADDR2MUX));
  Buffer buffer_103 (.in(buffer2b_10_out), .out_2(LD_MAR));  // open: out
  Buffer buffer_104 (.in(buffer_76_out), .out(buffer_104_out), .out_2(MARMUX));
  Buffer buffer_105 (.in(buffer_79_out), .out(buffer_105_out), .out_2(MARMUX));
  Buffer buffer_106 (.in(buffer_82_out), .out(buffer_106_out), .out_2(MARMUX));
  Buffer buffer_107 (.in(buffer2b_5_out), .out(buffer_107_out), .out_2(GateMARMUX));
  Buffer buffer_108 (.in(buffer_85_out), .out(buffer_108_out), .out_2(MARMUX));
  or or_12 (ASK, command_45_select_line, command_46_select_line);
  Buffer buffer_109 (.in(buffer_92_out), .out(buffer_109_out), .out_2(LD_OR));
  Buffer buffer_110 (.in(buffer_109_out), .out(buffer_110_out), .out_2(LD_REG));
  Buffer2b buffer2b_11 (.Value(2'b01), .in(buffer_93_out), .out(buffer2b_11_out), .out_3(ALUK));
  Buffer buffer_111 (.in(buffer_95_out), .out(buffer_111_out), .out_2(GateHDD));
  Buffer3b buffer3b_6 (.Value(IRin[11:9]), .in(buffer2b_7_out), .out(buffer3b_6_out), .out_3(DR));
  Buffer3b buffer3b_7 (.Value(IRin[8:6]), .in(buffer3b_6_out), .out(buffer3b_7_out), .out_3(SR1));
  Buffer2b buffer2b_12 (.Value(2'b01), .in(buffer_96_out), .out_3(PCMUX));  // open: out
  and and_34 (and_34_out, buffer2b_9_out, IRin[11]);
  and and_35 (and_35_out, ~IRin[11], buffer2b_9_out);  // AND_Gate
  Buffer3b buffer3b_8 (.Value(IRin[11:9]), .in(buffer_97_out), .out(buffer3b_8_out), .out_3(DR));
  Buffer3b buffer3b_9 (.Value(IRin[8:6]), .in(buffer3b_8_out), .out_3(SR1));  // open: out
  Buffer2b buffer2b_13 (.Value(2'b10), .in(buffer_98_out), .out_3(ADDR2MUX));  // open: out
  Buffer2b buffer2b_14 (.Value(2'b10), .in(buffer_100_out), .out_3(ADDR2MUX));  // open: out
  Buffer2b buffer2b_15 (.Value(2'b01), .in(buffer_112_out), .out(buffer2b_15_out), .out_3(ADDR2MUX));
  Buffer buffer_112 (.in(buffer_101_out), .out(buffer_112_out), .out_2(ADDR1MUX));
  Buffer2b buffer2b_16 (.Value(2'b10), .in(buffer_102_out), .out(buffer2b_16_out), .out_3(ADDR2MUX));
  Buffer3b buffer3b_10 (.Value(IRin[11:9]), .in(buffer2b_16_out), .out(buffer3b_10_out), .out_3(DR));
  Buffer buffer_113 (.in(buffer_104_out), .out(buffer_113_out), .out_2(ADDR1MUX));
  Buffer2b buffer2b_17 (.Value(2'b10), .in(buffer_105_out), .out_3(ADDR2MUX));  // open: out
  Buffer buffer_114 (.in(buffer_106_out), .out(buffer_114_out), .out_2(ADDR1MUX));
  Buffer buffer_115 (.in(buffer_116_out), .out(buffer_115_out), .out_2(ADDR1MUX));
  Buffer buffer_116 (.in(buffer_107_out), .out(buffer_116_out), .out_2(MARMUX));
  Buffer buffer_117 (.in(buffer_108_out), .out(buffer_117_out), .out_2(ADDR1MUX));
  Buffer3b buffer3b_11 (.Value(IRin[10:8]), .in(buffer_110_out), .out_3(DR));  // open: out
  Buffer3b buffer3b_12 (.Value(IRin[11:9]), .in(buffer2b_11_out), .out(buffer3b_12_out), .out_3(DR));
  Buffer3b buffer3b_13 (.Value(IRin[8:6]), .in(buffer3b_12_out), .out(buffer3b_13_out), .out_3(SR1));
  Buffer buffer_118 (.in(buffer_119_out), .out(HDDcheck));  // open: out_2
  Buffer buffer_119 (.in(buffer_111_out), .out(buffer_119_out), .out_2(LD_IR));
  Buffer3b buffer3b_14 (.Value(IRin[2:0]), .in(buffer3b_7_out), .out_3(SR2));  // open: out
  Buffer2b buffer2b_18 (.Value(2'b11), .in(and_34_out), .out_3(ADDR2MUX));  // open: out
  Buffer buffer_120 (.in(and_35_out), .out(buffer_120_out), .out_2(ADDR1MUX));
  Buffer3b buffer3b_15 (.Value(IRin[8:6]), .in(buffer2b_15_out), .out(buffer3b_15_out), .out_3(DR));
  Buffer buffer_121 (.in(buffer3b_10_out), .out_2(LD_REG));  // open: out
  Buffer3b buffer3b_16 (.Value(IRin[11:9]), .in(buffer_113_out), .out_3(SR1));  // open: out
  Buffer3b buffer3b_17 (.Value(IRin[11:9]), .in(buffer_114_out), .out_3(SR1));  // open: out
  Buffer3b buffer3b_18 (.Value(IRin[8:6]), .in(buffer_115_out), .out_3(SR1));  // open: out
  Buffer3b buffer3b_19 (.Value(IRin[11:9]), .in(buffer_117_out), .out_3(SR1));  // open: out
  Buffer3b buffer3b_20 (.Value(IRin[2:0]), .in(buffer3b_13_out), .out_3(SR2));  // open: out
  Buffer buffer_122 (.in(IRin[5]), .out_2(SR2MUX));  // open: out
  Buffer buffer_123 (.in(buffer3b_15_out), .out_2(LD_REG));  // open: out
  Buffer buffer_124 (.in(IRin[5]), .out_2(SR2MUX));  // open: out
  Buffer3b buffer3b_21 (.Value(IRin[8:6]), .in(buffer_120_out), .out_3(SR1));  // open: out
  Clock clock_1 (.out(clock_1_out));
  and and_36 (Clock, clock_1_out, ~ENFORCED_STOP, R);  // AND_Gate
  Pull_Resistor pull_resistor_1 (.node(DR));
  Pull_Resistor pull_resistor_2 (.node(LD_REG));
  Pull_Resistor pull_resistor_3 (.node(SR1));
  Pull_Resistor pull_resistor_4 (.node(SR2));
  Pull_Resistor pull_resistor_5 (.node(ALUK));
  Pull_Resistor pull_resistor_6 (.node(SR2MUX));
  Pull_Resistor pull_resistor_7 (.node(LD_CC));
  Pull_Resistor pull_resistor_8 (.node(LD_IR));
  Pull_Resistor pull_resistor_9 (.node(LD_MDR));
  Pull_Resistor pull_resistor_10 (.node(LD_MAR));
  Pull_Resistor pull_resistor_11 (.node(MIO_EN));
  Pull_Resistor pull_resistor_12 (.node(MEM_EN));
  Pull_Resistor pull_resistor_13 (.node(MEM_RW));
  Pull_Resistor pull_resistor_14 (.node(GateMDR));
  Pull_Resistor pull_resistor_15 (.node(GateALU));
  Pull_Resistor pull_resistor_16 (.node(GateMARMUX));
  Pull_Resistor pull_resistor_17 (.node(GatePC));
  Pull_Resistor pull_resistor_18 (.node(LD_PC));
  Pull_Resistor pull_resistor_19 (.node(PCMUX));
  Pull_Resistor pull_resistor_20 (.node(MARMUX));
  Pull_Resistor pull_resistor_21 (.node(ADDR2MUX));
  Pull_Resistor pull_resistor_22 (.node(ADDR1MUX));
  Pull_Resistor pull_resistor_23 (.node(MEM_HDD));
  Pull_Resistor pull_resistor_24 (.node(GateHDD));
  Pull_Resistor pull_resistor_25 (.node(LD_PRINT));
  Pull_Resistor pull_resistor_26 (.node(LD_READ));
  Pull_Resistor pull_resistor_27 (.node(LD_OR));
  Pull_Resistor pull_resistor_28 (.node(GateKR));
  Pull_Resistor pull_resistor_29 (.node(CKEY));
  Pull_Resistor pull_resistor_30 (.node(ASK));
  Pull_Resistor pull_resistor_31 (.node(mainOFF));

  // Other names for the same wires on the sheet: IR[15:0] = IRin; NZP[2:0] = NZPin; Power = R
endmodule

module REG_FILE (
  input  reset,
  input  [15:0] \input ,
  input  [2:0] DR,
  input  LD_REG,
  input  Clock,
  input  [2:0] SR2,
  input  [2:0] SR1,
  output [15:0] out_8,
  output [15:0] out_9,
  output [15:0] out_10,
  output [15:0] out_11,
  output [15:0] out_12,
  output [15:0] out_13,
  output [15:0] out_14,
  output [15:0] out_15,
  output [15:0] SR2_2,
  output [15:0] SR1_2
);

  wire ld_1__0, ld_1__1, ld_1__2, ld_1__3, ld_1__4, ld_1__5, ld_1__6, ld_1__7;

  LD ld_1 (
    .DR(DR), ._7(ld_1__7), ._6(ld_1__6), ._5(ld_1__5), ._4(ld_1__4), ._3(ld_1__3), ._2(ld_1__2),
    ._1(ld_1__1), ._0(ld_1__0), .LD_REG(LD_REG));
  Register #(.width(16)) _0 (.D(\input ), .en(ld_1__0), .Q(out_8), .clk(Clock), .clr(reset));
  Register #(.width(16)) _1 (.D(\input ), .en(ld_1__1), .Q(out_9), .clk(Clock), .clr(reset));
  Register #(.width(16)) _2 (.D(\input ), .en(ld_1__2), .Q(out_10), .clk(Clock), .clr(reset));
  Register #(.width(16)) _3 (.D(\input ), .en(ld_1__3), .Q(out_11), .clk(Clock), .clr(reset));
  REG_MUX reg_mux_1 (
    .in_1(SR2), ._0(out_8), ._1(out_9), ._2(out_10), ._3(out_11), ._4(out_12), ._5(out_13), ._6(out_14),
    ._7(out_15), .out_10(SR2_2));
  Register #(.width(16)) _4 (.D(\input ), .en(ld_1__4), .Q(out_12), .clk(Clock), .clr(reset));
  Register #(.width(16)) _5 (.D(\input ), .en(ld_1__5), .Q(out_13), .clk(Clock), .clr(reset));
  Register #(.width(16)) _6 (.D(\input ), .en(ld_1__6), .Q(out_14), .clk(Clock), .clr(reset));
  Register #(.width(16)) _7 (.D(\input ), .en(ld_1__7), .Q(out_15), .clk(Clock), .clr(reset));
  Pull_Resistor pull_resistor_1 (.node(out_8));
  Pull_Resistor pull_resistor_2 (.node(out_9));
  Pull_Resistor pull_resistor_3 (.node(out_10));
  Pull_Resistor pull_resistor_4 (.node(out_11));
  Pull_Resistor pull_resistor_5 (.node(out_12));
  Pull_Resistor pull_resistor_6 (.node(out_13));
  Pull_Resistor pull_resistor_7 (.node(out_14));
  Pull_Resistor pull_resistor_8 (.node(out_15));
  REG_MUX reg_mux_2 (
    .in_1(SR1), ._0(out_8), ._1(out_9), ._2(out_10), ._3(out_11), ._4(out_12), ._5(out_13), ._6(out_14),
    ._7(out_15), .out_10(SR1_2));
endmodule

module LD (
  input  [2:0] DR,
  input  LD_REG,
  output _7,
  output _6,
  output _5,
  output _4,
  output _3,
  output _2,
  output _1,
  output _0
);

  wire and_1_out, and_2_out, and_3_out, and_4_out, and_5_out, and_6_out, and_7_out, and_8_out;

  and and_1 (and_1_out, DR[2], DR[1], ~DR[0]);  // AND_Gate
  and and_2 (and_2_out, DR[2], DR[1], DR[0]);
  and and_3 (and_3_out, DR[2], ~DR[1], DR[0]);  // AND_Gate
  and and_4 (and_4_out, DR[2], ~DR[1], ~DR[0]);  // AND_Gate
  and and_5 (and_5_out, ~DR[2], DR[1], DR[0]);  // AND_Gate
  and and_6 (and_6_out, ~DR[2], DR[1], ~DR[0]);  // AND_Gate
  and and_7 (and_7_out, ~DR[2], ~DR[1], ~DR[0]);  // AND_Gate
  and and_8 (and_8_out, ~DR[2], ~DR[1], DR[0]);  // AND_Gate
  and and_9 (_7, and_2_out, LD_REG);
  and and_10 (_6, and_1_out, LD_REG);
  and and_11 (_5, and_3_out, LD_REG);
  and and_12 (_4, and_4_out, LD_REG);
  and and_13 (_3, and_5_out, LD_REG);
  and and_14 (_2, and_6_out, LD_REG);
  and and_15 (_1, and_8_out, LD_REG);
  and and_16 (_0, and_7_out, LD_REG);
endmodule

module MUX2 (
  input  [15:0] _1,
  input  in_2,
  input  [15:0] _0,
  output [15:0] out_4
);

  Transistor #(.\type ("n"), .gate("br"), .width(16)) transistor_1 (.in(_1), .out(out_4), .gate(in_2));
  Transistor #(.width(16)) transistor_2 (.in(_0), .out(out_4), .gate(in_2));
endmodule

module ALU (
  input  [15:0] SR1,
  input  [15:0] in_2,
  input  [1:0] ALUK,
  output [15:0] out_4
);

  wire ADD_out, and_2_out, AND_3_out, NOT_out;
  wire [15:0] adder_1_out, and_1_out, and_4_out, and_5_out, and_6_out, and_7_out, bit_extender_1_out,
       bit_extender_2_out, bit_extender_3_out, bit_extender_4_out, not_2_out;

  assign and_1_out = SR1 & in_2;  // AND_Gate and_1, 16 bits wide
  and and_2 (and_2_out, ~ALUK[0], ~ALUK[1]);  // AND_Gate
  and ADD (ADD_out, ALUK[0], ~ALUK[1]);  // AND_Gate
  and AND_3 (AND_3_out, ~ALUK[0], ALUK[1]);  // AND_Gate
  and NOT (NOT_out, ALUK[0], ALUK[1]);
  Adder #(.width(16)) adder_1 (.a(SR1), .b(in_2), .out(adder_1_out));  // open: cin, cout
  assign not_2_out = ~SR1;  // NOT_Gate not_2, 16 bits wide
  assign bit_extender_1_out = {{15{and_2_out}}, and_2_out};  // Bit_Extender bit_extender_1
  assign bit_extender_2_out = {{15{ADD_out}}, ADD_out};  // Bit_Extender bit_extender_2
  assign bit_extender_3_out = {{15{AND_3_out}}, AND_3_out};  // Bit_Extender bit_extender_3
  assign bit_extender_4_out = {{15{NOT_out}}, NOT_out};  // Bit_Extender bit_extender_4
  assign and_4_out = SR1 & bit_extender_1_out;  // AND_Gate and_4, 16 bits wide
  assign and_5_out = adder_1_out & bit_extender_2_out;  // AND_Gate and_5, 16 bits wide
  assign and_6_out = and_1_out & bit_extender_3_out;  // AND_Gate and_6, 16 bits wide
  assign and_7_out = not_2_out & bit_extender_4_out;  // AND_Gate and_7, 16 bits wide
  assign out_4 = and_4_out | and_5_out | and_6_out | and_7_out;  // OR_Gate or_1, 16 bits wide
endmodule

module BitStore (
  input  LD,
  input  Clock,
  input  _1,
  input  clear,
  output Current,
  output LD_Next
);

  wire and_1_out, and_2_out, s_r_ff_1_qn;

  and and_1 (and_1_out, ~LD_Next, _1);  // AND_Gate
  S_R_Flip_Flop s_r_ff_1 (
    .S(and_1_out), .clk(Clock), .R(and_2_out), .Q(Current), .Qn(s_r_ff_1_qn), .reset(clear), .en(LD));  // open: preset
  not not_1 (LD_Next, s_r_ff_1_qn);
  and and_2 (and_2_out, LD_Next, _1);
endmodule

module REG_MUX (
  input  [2:0] in_1,
  input  [15:0] _0,
  input  [15:0] _1,
  input  [15:0] _2,
  input  [15:0] _3,
  input  [15:0] _4,
  input  [15:0] _5,
  input  [15:0] _6,
  input  [15:0] _7,
  output [15:0] out_10
);

  wire and_1_out, and_2_out, and_3_out, and_4_out, and_5_out, and_6_out, and_7_out, and_8_out;
  wire [15:0] and_9_out, and_10_out, and_11_out, and_12_out, and_13_out, and_14_out, and_15_out, and_16_out,
       bit_extender_1_out, bit_extender_2_out, bit_extender_3_out, bit_extender_4_out, bit_extender_5_out,
       bit_extender_6_out, bit_extender_7_out, bit_extender_8_out;

  and and_1 (and_1_out, in_1[2], in_1[1], in_1[0]);
  assign bit_extender_1_out = {{15{and_1_out}}, and_1_out};  // Bit_Extender bit_extender_1
  and and_2 (and_2_out, in_1[2], ~in_1[1], in_1[0]);  // AND_Gate
  and and_3 (and_3_out, in_1[2], in_1[1], ~in_1[0]);  // AND_Gate
  assign bit_extender_2_out = {{15{and_2_out}}, and_2_out};  // Bit_Extender bit_extender_2
  assign bit_extender_3_out = {{15{and_3_out}}, and_3_out};  // Bit_Extender bit_extender_3
  and and_4 (and_4_out, ~in_1[2], in_1[1], in_1[0]);  // AND_Gate
  and and_5 (and_5_out, in_1[2], ~in_1[1], ~in_1[0]);  // AND_Gate
  assign bit_extender_4_out = {{15{and_4_out}}, and_4_out};  // Bit_Extender bit_extender_4
  assign bit_extender_5_out = {{15{and_5_out}}, and_5_out};  // Bit_Extender bit_extender_5
  and and_6 (and_6_out, ~in_1[2], in_1[1], ~in_1[0]);  // AND_Gate
  and and_7 (and_7_out, ~in_1[2], ~in_1[1], in_1[0]);  // AND_Gate
  assign bit_extender_6_out = {{15{and_7_out}}, and_7_out};  // Bit_Extender bit_extender_6
  assign bit_extender_7_out = {{15{and_6_out}}, and_6_out};  // Bit_Extender bit_extender_7
  and and_8 (and_8_out, ~in_1[2], ~in_1[1], ~in_1[0]);  // AND_Gate
  assign bit_extender_8_out = {{15{and_8_out}}, and_8_out};  // Bit_Extender bit_extender_8
  // Probe on bit_extender_6_out
  assign and_9_out = bit_extender_8_out & _0;  // AND_Gate and_9, 16 bits wide
  assign and_10_out = bit_extender_6_out & _1;  // AND_Gate and_10, 16 bits wide
  assign and_11_out = bit_extender_7_out & _2;  // AND_Gate and_11, 16 bits wide
  assign and_12_out = bit_extender_4_out & _3;  // AND_Gate and_12, 16 bits wide
  assign and_13_out = bit_extender_5_out & _4;  // AND_Gate and_13, 16 bits wide
  assign and_14_out = bit_extender_2_out & _5;  // AND_Gate and_14, 16 bits wide
  assign and_15_out = bit_extender_3_out & _6;  // AND_Gate and_15, 16 bits wide
  assign and_16_out = bit_extender_1_out & _7;  // AND_Gate and_16, 16 bits wide
  assign out_10 = and_9_out | and_10_out | and_11_out | and_12_out | and_13_out | and_14_out | and_15_out | and_16_out;  // OR_Gate or_1, 16 bits wide
endmodule

module LOGIC (
  input  [15:0] in_1,
  output N,
  output Z,
  output P
);

  wire nor_1_out, transistor_3_out;

  Pull_Resistor pull_resistor_1 (.node(in_1));
  nor nor_1 (nor_1_out, in_1[0], in_1[1], in_1[2], in_1[3], in_1[4], in_1[5], in_1[6], in_1[7], in_1[8], in_1[9], in_1[10], in_1[11], in_1[12], in_1[13], in_1[14], in_1[15]);
  Transistor #(.\type ("n")) transistor_1 (.in(1'b1), .out(N), .gate(in_1[15]));
  Pull_Resistor pull_resistor_2 (.node(N));
  Transistor #(.\type ("n")) transistor_2 (.in(1'b1), .out(Z), .gate(nor_1_out));
  Pull_Resistor pull_resistor_3 (.node(Z));
  Pull_Resistor pull_resistor_4 (.node(P));
  Transistor transistor_3 (.in(1'b1), .out(transistor_3_out), .gate(in_1[15]));
  Transistor transistor_4 (.in(transistor_3_out), .out(P), .gate(nor_1_out));
endmodule

module Gate (
  input  LD,
  input  [15:0] Data,
  output [15:0] Out
);

  Transistor #(.\type ("n"), .width(16)) transistor_1 (.in(Data), .out(Out), .gate(LD));
endmodule

module Command (
  input  Start,
  input  CommandON,
  input  Clock,
  input  On,
  input  in_5,
  output Select_Line,
  output On_2
);

  wire and_1_out, bitstore_1_ld_next, not_1_out, not_2_out, or_2_out, or_3_out;

  or or_1 (On_2, On, bitstore_1_ld_next);
  or or_2 (or_2_out, and_1_out, bitstore_1_ld_next);
  not not_1 (not_1_out, Clock);
  BitStore bitstore_1 (
    .Clock(not_1_out), ._1(or_2_out), .Current(Select_Line), .LD_Next(bitstore_1_ld_next), .clear(or_3_out));  // open: LD
  or or_3 (or_3_out, not_2_out, in_5);
  not not_2 (not_2_out, On_2);
  and and_1 (and_1_out, CommandON, Start);
endmodule

module _1 (
  input  [15:0] in_1,
  output [15:0] out_2
);

  Adder #(.width(16)) adder_1 (.a(in_1), .b(16'h1), .out(out_2));  // open: cin, cout
endmodule

module MUX4 (
  input  [1:0] in_1,
  input  [15:0] _3,
  input  [15:0] _2,
  input  [15:0] _1,
  input  [15:0] _0,
  output [15:0] out_6
);

  wire and_1_out, and_2_out, and_3_out, and_4_out;
  wire [15:0] and_5_out, and_6_out, and_7_out, and_8_out, bit_extender_1_out, bit_extender_2_out,
       bit_extender_3_out, bit_extender_4_out;

  assign bit_extender_1_out = {{15{and_1_out}}, and_1_out};  // Bit_Extender bit_extender_1
  and and_1 (and_1_out, in_1[0], in_1[1]);
  and and_2 (and_2_out, ~in_1[0], in_1[1]);  // AND_Gate
  assign bit_extender_2_out = {{15{and_2_out}}, and_2_out};  // Bit_Extender bit_extender_2
  assign bit_extender_3_out = {{15{and_3_out}}, and_3_out};  // Bit_Extender bit_extender_3
  and and_3 (and_3_out, in_1[0], ~in_1[1]);  // AND_Gate
  and and_4 (and_4_out, ~in_1[0], ~in_1[1]);  // AND_Gate
  assign bit_extender_4_out = {{15{and_4_out}}, and_4_out};  // Bit_Extender bit_extender_4
  assign and_5_out = bit_extender_1_out & _3;  // AND_Gate and_5, 16 bits wide
  assign and_6_out = bit_extender_2_out & _2;  // AND_Gate and_6, 16 bits wide
  assign and_7_out = bit_extender_3_out & _1;  // AND_Gate and_7, 16 bits wide
  assign and_8_out = bit_extender_4_out & _0;  // AND_Gate and_8, 16 bits wide
  assign out_6 = and_5_out | and_6_out | and_7_out | and_8_out;  // OR_Gate or_1, 16 bits wide
endmodule

module ADD (
  input  [15:0] in_1,
  input  [15:0] in_2,
  output [15:0] out_3
);

  Adder #(.width(16)) adder_1 (.a(in_1), .b(in_2), .out(out_3));  // open: cin, cout
endmodule

module Buffer (
  input  in,
  output out_2,
  output out
);

  Transistor #(.\type ("n")) transistor_1 (.in(in), .out(out_2), .gate(in));
  Pull_Resistor pull_resistor_1 (.node(out));
  Transistor #(.\type ("n")) transistor_2 (.in(out_2), .out(out), .gate(1'b1));
endmodule

module Buffer2b (
  input  [1:0] Value,
  input  in,
  output [1:0] out_3,
  output out
);

  wire transistor_2_out;

  Transistor #(.\type ("n"), .width(2)) transistor_1 (.in(Value), .out(out_3), .gate(in));
  Transistor #(.\type ("n")) transistor_2 (.in(in), .out(transistor_2_out), .gate(in));
  Transistor #(.\type ("n")) transistor_3 (.in(transistor_2_out), .out(out), .gate(1'b1));
  Pull_Resistor pull_resistor_1 (.node(out));
endmodule

module Buffer3b (
  input  [2:0] Value,
  input  in,
  output [2:0] out_3,
  output out
);

  wire transistor_1_out;

  Transistor #(.\type ("n")) transistor_1 (.in(in), .out(transistor_1_out), .gate(in));
  Transistor #(.\type ("n"), .width(3)) transistor_2 (.in(Value), .out(out_3), .gate(in));
  Transistor #(.\type ("n")) transistor_3 (.in(transistor_1_out), .out(out), .gate(1'b1));
  Pull_Resistor pull_resistor_1 (.node(out));
endmodule

module Buffer4b (
  input  [3:0] Value,
  input  in,
  output [3:0] out_3,
  output out
);

  wire transistor_1_out;

  Transistor #(.\type ("n")) transistor_1 (.in(in), .out(transistor_1_out), .gate(in));
  Transistor #(.\type ("n"), .width(4)) transistor_2 (.in(Value), .out(out_3), .gate(in));
  Transistor #(.\type ("n")) transistor_3 (.in(transistor_1_out), .out(out), .gate(1'b1));
  Pull_Resistor pull_resistor_1 (.node(out));
endmodule

module HexConvert (
  input  in_1,
  input  [3:0] in_2,
  output [6:0] out_3
);

  Multiplexer #(.select(4), .width(7)) multiplexer_1 (
    .in0(7'b0110000), .in1(7'b0110001), .in2(7'b0110010), .in3(7'b0110011), .in4(7'b0110100),
    .in5(7'b0110101), .in6(7'b0110110), .in7(7'b0110111), .in8(7'b0111000), .in9(7'b0111001),
    .in10(7'b1000001), .in11(7'b1000010), .in12(7'b1000011), .in13(7'b1000100), .in14(7'b1000101),
    .in15(7'b1000110), .out(out_3), .sel(in_2), .en(in_1));
endmodule
