// Logisim project Calculator.circ as structural Verilog: 5 circuits, main circuit main
module main (
  input  in_1,
  input  [15:0] A,
  input  [15:0] B,
  output [15:0] out_4,
  output out_5
);

  wire add8b_1_out_5;

  ADD8b add8b_1 (.in_1(in_1), .A(A[7:0]), .B(B[7:0]), .out_4(out_4[7:0]), .out_5(add8b_1_out_5));
  ADD8b add8b_2 (.in_1(add8b_1_out_5), .A(A[15:8]), .B(B[15:8]), .out_4(out_4[15:8]), .out_5(out_5));
  LED led_1 (.in(out_5));
endmodule

module Add3 (
  input  in_1,
  input  in_2,
  input  in_3,
  output out_4,
  output out_5
);

  wire and_1_out, nor_1_out, xnor_1_out, xor_1_out, xor_2_out;

  ExactlyOne xor_1 (.out(xor_1_out), .in0(in_1), .in1(in_2), .in2(in_3));
  nor nor_1 (nor_1_out, in_1, in_2, in_3);
  xnor xnor_1 (xnor_1_out, in_1, in_2, in_3);
  and and_1 (and_1_out, in_1, in_2, in_3);
  xor xor_2 (xor_2_out, nor_1_out, xnor_1_out);
  or or_1 (out_4, xor_1_out, and_1_out);
  or or_2 (out_5, xor_2_out, and_1_out);
endmodule

module Add4b (
  input  [3:0] A,
  input  in_2,
  input  [3:0] B,
  output [3:0] R,
  output out_5
);

  wire add3_1_out_5, add3_2_out_5, add3_3_out_5;

  Add3 add3_1 (.in_3(in_2), .in_2(A[0]), .in_1(B[0]), .out_4(R[0]), .out_5(add3_1_out_5));
  Add3 add3_2 (.in_3(add3_1_out_5), .in_2(B[1]), .in_1(A[1]), .out_4(R[1]), .out_5(add3_2_out_5));
  Add3 add3_3 (.in_3(add3_2_out_5), .in_2(A[2]), .in_1(B[2]), .out_4(R[2]), .out_5(add3_3_out_5));
  Add3 add3_4 (.in_3(add3_3_out_5), .in_2(A[3]), .in_1(B[3]), .out_4(R[3]), .out_5(out_5));
endmodule

module ADD8b (
  input  in_1,
  input  [7:0] A,
  input  [7:0] B,
  output [7:0] out_4,
  output out_5
);

  wire add4b_1_out_5;

  Add4b add4b_1 (.A(A[3:0]), .B(B[3:0]), .R(out_4[3:0]), .out_5(add4b_1_out_5), .in_2(in_1));
  Add4b add4b_2 (.A(A[7:4]), .B(B[7:4]), .R(out_4[7:4]), .out_5(out_5), .in_2(add4b_1_out_5));
  LED led_1 (.in(out_5));
endmodule

// 0
module Add16b (
  output [7:0] out_1,
  output [7:0] out_2
);

  wire _0_out, _1_out, _2_out, _3_out, _4_out, _5_out, _6_out, _7_out, _8_out, _9_out, and_1_out, and_2_out,
       and_3_out, and_4_out, and_5_out, and_6_out, and_7_out, and_8_out, and_9_out, and_10_out, clock_1_out,
       or_1_out;
  wire [7:0] and_11_out, and_12_out, and_13_out, and_14_out, and_15_out, and_16_out, and_17_out, and_18_out,
       and_19_out, and_20_out, bit_extender_1_out, bit_extender_2_out, bit_extender_3_out,
       bit_extender_4_out, bit_extender_5_out, bit_extender_6_out, bit_extender_7_out, bit_extender_8_out,
       bit_extender_9_out, bit_extender_10_out;

  Button _1 (.out(_1_out));
  Button _4 (.out(_4_out));
  Button _7 (.out(_7_out));
  Button _3 (.out(_3_out));
  Button _2 (.out(_2_out));
  Button _5 (.out(_5_out));
  Button _6 (.out(_6_out));
  Button _9 (.out(_9_out));
  Button _8 (.out(_8_out));
  Button _0 (.out(_0_out));
  and and_1 (and_1_out, 1'b1, _0_out);
  and and_2 (and_2_out, 1'b1, _9_out);
  and and_3 (and_3_out, 1'b1, _8_out);
  and and_4 (and_4_out, 1'b1, _7_out);
  and and_5 (and_5_out, 1'b1, _6_out);
  and and_6 (and_6_out, 1'b1, _5_out);
  and and_7 (and_7_out, 1'b1, _4_out);
  and and_8 (and_8_out, 1'b1, _3_out);
  and and_9 (and_9_out, 1'b1, _2_out);
  and and_10 (and_10_out, 1'b1, _1_out);
  assign bit_extender_1_out = {{7{and_1_out}}, and_1_out};  // Bit_Extender bit_extender_1
  assign and_11_out = bit_extender_1_out & 8'h77;  // AND_Gate and_11, 8 bits wide
  assign bit_extender_2_out = {{7{and_2_out}}, and_2_out};  // Bit_Extender bit_extender_2
  assign and_12_out = bit_extender_2_out & 8'h6f;  // AND_Gate and_12, 8 bits wide
  assign bit_extender_3_out = {{7{and_3_out}}, and_3_out};  // Bit_Extender bit_extender_3
  assign and_13_out = bit_extender_3_out & 8'h7f;  // AND_Gate and_13, 8 bits wide
  assign and_14_out = bit_extender_4_out & 8'h47;  // AND_Gate and_14, 8 bits wide
  assign bit_extender_4_out = {{7{and_4_out}}, and_4_out};  // Bit_Extender bit_extender_4
  assign and_15_out = bit_extender_5_out & 8'h7e;  // AND_Gate and_15, 8 bits wide
  assign bit_extender_5_out = {{7{and_5_out}}, and_5_out};  // Bit_Extender bit_extender_5
  assign bit_extender_6_out = {{7{and_6_out}}, and_6_out};  // Bit_Extender bit_extender_6
  assign and_16_out = bit_extender_6_out & 8'h6e;  // AND_Gate and_16, 8 bits wide
  assign and_17_out = bit_extender_7_out & 8'h4d;  // AND_Gate and_17, 8 bits wide
  assign bit_extender_7_out = {{7{and_7_out}}, and_7_out};  // Bit_Extender bit_extender_7
  assign and_18_out = bit_extender_8_out & 8'h6b;  // AND_Gate and_18, 8 bits wide
  assign bit_extender_8_out = {{7{and_8_out}}, and_8_out};  // Bit_Extender bit_extender_8
  assign bit_extender_9_out = {{7{and_9_out}}, and_9_out};  // Bit_Extender bit_extender_9
  assign and_19_out = bit_extender_9_out & 8'h3b;  // AND_Gate and_19, 8 bits wide
  assign bit_extender_10_out = {{7{and_10_out}}, and_10_out};  // Bit_Extender bit_extender_10
  assign and_20_out = bit_extender_10_out & 8'h41;  // AND_Gate and_20, 8 bits wide
  or or_1 (or_1_out, _0_out, _9_out, _8_out, _7_out, _6_out, _5_out, _4_out, _3_out, _2_out, _1_out);
  assign out_2 = and_11_out | and_12_out | and_13_out | and_14_out | and_15_out | and_16_out | and_17_out | and_18_out | and_19_out | and_20_out;  // OR_Gate or_2, 8 bits wide
  Register #(.trigger("high")) register_1 (.D(out_2), .en(or_1_out), .Q(out_1), .clk(clock_1_out));  // open: clr
  Clock clock_1 (.out(clock_1_out));
  _7_Segment_Display u_7_segment_display_1 (
    .g(out_1[3]), .f(out_1[2]), .a(out_1[1]), .b(out_1[0]), .e(out_1[4]), .d(out_1[5]), .c(out_1[6]),
    .dp(out_1[7]));
endmodule
